# Fritzing sketch Discovery_Door_Lock (saved by Fritzing 0.9.3b)

parts:
  U1 = NodeMCU V3.0
  S1 = Momentary Switch [part_number=Reset package=ksa_sealed_tac_switch]
  S2 = Momentary Switch [part_number=On package=ksa_sealed_tac_switch]
  S3 = Momentary Switch [part_number=Off package=ksa_sealed_tac_switch]
  U2 = XD-RF-5V [package=THT]
  R1 = Resistor [tolerance=±5% resistance=470 package=THT]
  R2 = Resistor [tolerance=±5% resistance=470 package=THT]
  R3 = Resistor [tolerance=±5% resistance=470 package=THT]
  J1 = Basic Servo
  LED1 = LED - 3mm [color="Red (633nm)" package="3 mm [THT]"]
  LED2 = LED - 3mm [color="Green (565nm)" package="3 mm [THT]"]
  R4 = Resistor [tolerance=±5% resistance=470 package=THT]
  R5 = Resistor [tolerance=±5% resistance=470 package=THT]
  J2 = Piezo Speaker
  BAT1 = LIPO-1000mAh [package=lipo-1000]

nets:
  N1: U1.D0, J2.pin2
  N2: U1.D1, R2.Pin_0
  N3: U1.D2, J1.pulse
  N4: U1.D3, U2.DATA
  N5: U1.D5, S3.1, R3.Pin_0
  N6: U1.D6, R4.Pin_0
  N7: U1.D7, S1.1, R1.Pin_0
  N8: U1.D8, R5.Pin_0
  N9: U1.GND#13, U1.GND#33, J2.pin1
  N10: U1.VU, S1.4, S2.4, S3.4, U2.VCC, BAT1.+
  N11: U1.GND#41, U2.GND
  N12: J1.gnd, BAT1.-
  N13: LED1.anode, R5.Pin_1
  N14: LED2.anode, R4.Pin_1

custom parts:
  NodeMCU V3.0: ESP8266 based NodeMCU
  XD-RF-5V: This is 433Mhz RF transmitter with receiver kit for Arduino ARM MCU wireless Application environment: Remote control switch, receiver module, motorcycles, automobile anti-theft products, home security products, electric doors, shutter doors, windows, remote control socket, remote control LED, remote audio remote control electric doors, garage door remote control, remote control retractable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
